# Fritzing sketch MainSCH (saved by Fritzing 1.0.3b)
breadboards: 1

parts:
  Controller = Arduino Uno (Rev3)
  Temperature_Sensor = TMP36 [package=to-92]
  R1 = Resistor [tolerance=±5% power=0.25W resistance=470 package=THT]
  Part1 = Soil Moisture Sensor
  SolarCell = S1133 Si Photodiode [package="8mm Ceramic [THT]"]
  WaterPump = DC Motor [voltage_(max)=6V voltage_(min)=3V]
  pumpSwithcTR = NPN-Transistor [package="TO92 [THT]"]
  SolarFollowerMotor = Stepper Motor - Bipolar
  StepperMController = Pololu A4988 [package=SO16]

nets:
  N1: Controller.A0, Part1.SIG
  N2: Controller.A1, SolarCell.cathode
  N3: Controller.A3, pumpSwithcTR.B
  N4: Controller.D10_PWM/SS, StepperMController.STEP
  N5: Controller.D11_PWM/MOSI, StepperMController.DIR
  GND: Controller.GND, Temperature_Sensor.GND, Part1.GND, SolarCell.anode, pumpSwithcTR.E, StepperMController.GND
  N6: Controller.D4, Temperature_Sensor.VOUT, R1.Pin_1
  N7: Controller.D7, Part1.VCC
  12V: Controller.VIN, WaterPump.pin_1, StepperMController.VMOT
  5V: Temperature_Sensor.VCC, R1.Pin_0, StepperMController.VDD
  N8: WaterPump.pin_2, pumpSwithcTR.C
  N9: SolarFollowerMotor.A, StepperMController.2B
  N10: SolarFollowerMotor.C, StepperMController.2A
  N11: SolarFollowerMotor.B, StepperMController.1A
  N12: SolarFollowerMotor.D, StepperMController.1B
  N13: StepperMController.RESET, StepperMController.SLEEP
